# Fritzing sketch schemtic (saved by Fritzing 0.9.5d)
breadboards: 1

parts:
  U1 = DOIT Esp32 DevKit v1 (30 pins long, 11 pins width) [part_number=ESP32S-PIN30]
  LCD2 = LCD screen
  M1 = BMP280
  U1_2 = ESP32 [part_number=ESP32]  # not connected
  U1_3 = ESP32 [part_number=ESP32]  # not connected
  Part1 = Adafruit CCS811 [part_number="Adafruit #3566"]
  LCM1602_IIC2 = LCM1602 IIC [part_number="LCM1602 IIC" chip_label="LCM1602 IIC" package="DIP (Dual Inline) [THT]"]

nets:
  3V3: U1.3V3, Part1.3.3V, LCM1602_IIC2.VCC
  GND: U1.GND, M1.GND, Part1.GND, LCM1602_IIC2.GND
  N1: U1.D21, Part1.SDA, LCM1602_IIC2.SDA
  N2: U1.D22, Part1.SCL, LCM1602_IIC2.SCL
  VIN: U1.VIN, Part1.VCC
  VSS: LCD2.VSS, LCM1602_IIC2.VSS
  VDD: LCD2.VDD, LCM1602_IIC2.VDD
  N3: LCD2.V0, LCM1602_IIC2.V0
  N4: LCD2.RS, LCM1602_IIC2.RS
  N5: LCD2.R/W, LCM1602_IIC2.RW
  N6: LCD2.E, LCM1602_IIC2.E
  N7: LCD2.DB0, LCM1602_IIC2.D0
  N8: LCD2.DB1, LCM1602_IIC2.D1
  N9: LCD2.DB2, LCM1602_IIC2.D2
  N10: LCD2.DB3, LCD2.DB4, LCM1602_IIC2.D3, LCM1602_IIC2.D4
  N11: LCD2.DB5, LCM1602_IIC2.D5
  N12: LCD2.DB6, LCM1602_IIC2.D6
  N13: LCD2.DB7, LCM1602_IIC2.D7
  N14: LCD2.LED+, LCM1602_IIC2.A
  N15: LCD2.LED-, LCM1602_IIC2.K

custom parts:
  DOIT Esp32 DevKit v1 (30 pins long, 11 pins width): The DOIT Esp32 DevKit v1 is one of the development board created by DOIT to evaluate the ESP-WROOM-32 module. It is based on the ESP32 microcontroller that boasts Wifi, Bluetooth, Ethernet and Low Power support all in a single chip. (vanepp) made breadboard work, adjusted pin numbering and labels and reduced size of schematic and cleaned up pcb. This chip is 30pins long (2 x15) and 11 pins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
  BMP280: Temperature Humidity Barometric presure Sensor, I2C
  ESP32: Generic WiFi Module based on the ESP32 with onboard PCB antenna and UART communications
  Adafruit CCS811: Breathe easy - we finally have an I2C VOC/eCO2 sensor in the Adafruit shop! Add air quality monitoring to your project and with an Adafruit CCS811 Air Quality Sensor Breakout. This sensor from AMS is a gas sensor that can detect a wide range of Volatile Organic Compounds (VOCs) and is intended for indoor air quality monitoring. When connected to your microcontroller (running our library code)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
  LCM1602 IIC: I2C-Module to use a 1602 or 2004 LCD on with the wire.h libory Serial LCD Modul
